// Logisim project control.circ as structural Verilog: 1 circuit, main circuit main
module main (
  input  Go,
  input  Equal,
  input  product1,
  input  CLK,
  output lMultiplicand,
  output lMultiplier,
  output sMultiplier,
  output lProduct,
  output [1:0] sProduct,
  output lControl,
  output sControl,
  output lCout,
  output sCout
);

  wire and_1_out, and_2_out, and_3_out, and_4_out, and_5_out, and_6_out, and_7_out, not_1_out, not_2_out,
       not_3_out, not_4_out, not_5_out, not_6_out, not_7_out, not_8_out;
  wire [2:0] N0_out, STATE_q;

  not not_1 (not_1_out, Equal);
  not not_2 (not_2_out, product1);
  Register #(.width(3)) STATE (.D(N0_out), .en(1'b1), .Q(STATE_q), .clk(CLK));  // open: clr
  not not_3 (not_3_out, STATE_q[2]);
  not not_4 (not_4_out, STATE_q[1]);
  not not_5 (not_5_out, STATE_q[0]);
  and and_1 (and_1_out, not_3_out, STATE_q[1], not_5_out, not_2_out);
  and and_2 (and_2_out, not_3_out, STATE_q[1], STATE_q[0]);
  and and_3 (and_3_out, not_3_out, not_4_out, STATE_q[0]);
  and and_4 (and_4_out, not_3_out, STATE_q[1], not_5_out, product1);
  and and_5 (and_5_out, STATE_q[2], not_4_out, not_5_out, not_1_out);
  and and_6 (and_6_out, not_3_out, not_4_out, not_5_out, Go);
  and and_7 (and_7_out, not_3_out, STATE_q[1], not_5_out, product1);
  or N2 (N0_out[2], and_1_out, and_2_out);
  or N1 (N0_out[1], and_3_out, and_4_out, and_5_out);
  or N0 (N0_out[0], and_6_out, and_7_out);
  not not_6 (not_6_out, STATE_q[1]);
  not not_7 (not_7_out, STATE_q[2]);
  not not_8 (not_8_out, STATE_q[0]);
  and _001 (lMultiplicand, not_7_out, not_6_out, STATE_q[0]);
  and _011 (sCout, not_7_out, STATE_q[1], STATE_q[0]);
  and _100 (sControl, STATE_q[2], not_6_out, not_6_out);
  or or_1 (lMultiplier, lMultiplicand, sControl);
  or or_2 (lProduct, lMultiplicand, sCout, sControl);
  or or_3 (lControl, lMultiplicand, sControl);
  or or_4 (lCout, lMultiplicand, sCout);

  assign sMultiplier = sControl;
  assign sProduct = {sControl, sCout};

  // Notes on the sheet:
  //   prdct1'
endmodule
