// Logisim project datapath.circ as structural Verilog: 6 circuits, main circuit main
module main (
  input  [31:0] Multiplicand,
  input  lcout,
  input  lMultiplicand,
  input  sCout,
  input  [31:0] Multiplier,
  input  lMultiplier,
  input  sMultiplier,
  input  lProduct,
  input  [1:0] sProduct,
  input  lControl,
  input  sControl,
  input  Clock,
  output [31:0] RESULTM,
  output [31:0] RESULTP,
  output product1,
  output Equal
);

  wire C_out_q, multiplexer_4_out, n32_bit_adder_1_c_out;
  wire [5:0] Control_q, multiplexer_3_out, n6_bit_adder_1_sum;
  wire [31:0] multiplexer_1_out, multiplexer_2_out, Multiplicand_q, n32_bit_adder_1_sum,
       n64_bit_shifter_1_multiplier_2, n64_bit_shifter_1_product_2;

  Register #(.width(32)) u_Multiplicand (
    .D(Multiplicand), .en(lMultiplicand), .Q(Multiplicand_q), .clk(Clock));  // open: clr
  Multiplexer #(.width(32), .enable("false")) multiplexer_1 (
    .in0(Multiplier), .in1(n64_bit_shifter_1_multiplier_2), .out(multiplexer_1_out), .sel(sMultiplier));
  Multiplexer #(.select(2), .width(32), .enable("false")) multiplexer_2 (
    .in0({32{1'b0}}), .in1(n32_bit_adder_1_sum), .in2(n64_bit_shifter_1_product_2), .out(multiplexer_2_out),
    .sel(sProduct));  // open: in3
  Multiplexer #(.width(6), .enable("false")) multiplexer_3 (
    .in0({6{1'b0}}), .in1(n6_bit_adder_1_sum), .out(multiplexer_3_out), .sel(sControl));
  Register #(.width(6)) Control (.D(multiplexer_3_out), .en(lControl), .Q(Control_q), .clk(Clock));  // open: clr
  Register #(.width(32)) u_Multiplier (
    .D(multiplexer_1_out), .en(lMultiplier), .Q({RESULTM[31:1], product1}), .clk(Clock));  // open: clr
  Register #(.width(32)) Product (.D(multiplexer_2_out), .en(lProduct), .Q(RESULTP), .clk(Clock));  // open: clr
  _6_bit_adder u_6_bit_adder_1 (.A(Control_q), .B(6'b000001), .Sum(n6_bit_adder_1_sum));  // open: C_out
  Multiplexer #(.enable("false")) multiplexer_4 (
    .in0(1'b0), .in1(n32_bit_adder_1_c_out), .out(multiplexer_4_out), .sel(sCout));
  equal equal_1 (.A(Control_q), .B(6'b011111), .Sum(Equal));
  _64_bit_shifter u_64_bit_shifter_1 (
    .Cout(C_out_q), .Product(RESULTP), .Multiplier({RESULTM[31:1], product1}),
    .Product_2(n64_bit_shifter_1_product_2), .Multiplier_2(n64_bit_shifter_1_multiplier_2));
  _32_bit_adder u_32_bit_adder_1 (
    .A(RESULTP), .B(Multiplicand_q), .Sum(n32_bit_adder_1_sum), .C_out(n32_bit_adder_1_c_out));
  Register #(.width(1)) C_out (.D(multiplexer_4_out), .en(lcout), .Q(C_out_q), .clk(Clock));  // open: clr

  assign RESULTM[0] = product1;

  // Notes on the sheet:
  //   6-bit adder
  //   comparator
  //   equal
  //   64-bit shifter
  //   32-bit adder
endmodule

module _1_bit_adder (
  input  A,
  input  B,
  input  C_in,
  output Sum,
  output C_out
);

  wire and_1_out, and_2_out, xor_1_out;

  xor xor_1 (xor_1_out, A, B);
  xor xor_2 (Sum, xor_1_out, C_in);
  and and_1 (and_1_out, xor_1_out, C_in);
  and and_2 (and_2_out, A, B);
  or or_1 (C_out, and_1_out, and_2_out);
endmodule

module _32_bit_adder (
  input  [31:0] A,
  input  [31:0] B,
  output C_out,
  output [31:0] Sum
);

  wire n1_bit_adder_1_c_out, n1_bit_adder_2_c_out, n1_bit_adder_3_c_out, n1_bit_adder_4_c_out,
       n1_bit_adder_5_c_out, n1_bit_adder_6_c_out, n1_bit_adder_7_c_out, n1_bit_adder_8_c_out,
       n1_bit_adder_9_c_out, n1_bit_adder_10_c_out, n1_bit_adder_11_c_out, n1_bit_adder_12_c_out,
       n1_bit_adder_13_c_out, n1_bit_adder_14_c_out, n1_bit_adder_15_c_out, n1_bit_adder_16_c_out,
       n1_bit_adder_17_c_out, n1_bit_adder_18_c_out, n1_bit_adder_19_c_out, n1_bit_adder_20_c_out,
       n1_bit_adder_21_c_out, n1_bit_adder_22_c_out, n1_bit_adder_23_c_out, n1_bit_adder_24_c_out,
       n1_bit_adder_25_c_out, n1_bit_adder_26_c_out, n1_bit_adder_27_c_out, n1_bit_adder_28_c_out,
       n1_bit_adder_29_c_out, n1_bit_adder_30_c_out, n1_bit_adder_31_c_out;

  _1_bit_adder u_1_bit_adder_1 (.A(A[0]), .B(B[0]), .C_in(1'b0), .Sum(Sum[0]), .C_out(n1_bit_adder_1_c_out));
  _1_bit_adder u_1_bit_adder_2 (
    .A(A[1]), .B(B[1]), .C_in(n1_bit_adder_1_c_out), .Sum(Sum[1]), .C_out(n1_bit_adder_2_c_out));
  _1_bit_adder u_1_bit_adder_3 (
    .A(A[2]), .B(B[2]), .C_in(n1_bit_adder_2_c_out), .Sum(Sum[2]), .C_out(n1_bit_adder_3_c_out));
  _1_bit_adder u_1_bit_adder_4 (
    .A(A[3]), .B(B[3]), .C_in(n1_bit_adder_3_c_out), .Sum(Sum[3]), .C_out(n1_bit_adder_4_c_out));
  _1_bit_adder u_1_bit_adder_5 (
    .A(A[4]), .B(B[4]), .C_in(n1_bit_adder_4_c_out), .Sum(Sum[4]), .C_out(n1_bit_adder_5_c_out));
  _1_bit_adder u_1_bit_adder_6 (
    .A(A[5]), .B(B[5]), .C_in(n1_bit_adder_5_c_out), .Sum(Sum[5]), .C_out(n1_bit_adder_6_c_out));
  _1_bit_adder u_1_bit_adder_7 (
    .A(A[6]), .B(B[6]), .C_in(n1_bit_adder_6_c_out), .Sum(Sum[6]), .C_out(n1_bit_adder_7_c_out));
  _1_bit_adder u_1_bit_adder_8 (
    .A(A[7]), .B(B[7]), .C_in(n1_bit_adder_7_c_out), .Sum(Sum[7]), .C_out(n1_bit_adder_8_c_out));
  _1_bit_adder u_1_bit_adder_9 (
    .A(A[8]), .B(B[8]), .C_in(n1_bit_adder_8_c_out), .Sum(Sum[8]), .C_out(n1_bit_adder_9_c_out));
  _1_bit_adder u_1_bit_adder_10 (
    .A(A[9]), .B(B[9]), .C_in(n1_bit_adder_9_c_out), .Sum(Sum[9]), .C_out(n1_bit_adder_10_c_out));
  _1_bit_adder u_1_bit_adder_11 (
    .A(A[10]), .B(B[10]), .C_in(n1_bit_adder_10_c_out), .Sum(Sum[10]), .C_out(n1_bit_adder_11_c_out));
  _1_bit_adder u_1_bit_adder_12 (
    .A(A[11]), .B(B[11]), .C_in(n1_bit_adder_11_c_out), .Sum(Sum[11]), .C_out(n1_bit_adder_12_c_out));
  _1_bit_adder u_1_bit_adder_13 (
    .A(A[12]), .B(B[12]), .C_in(n1_bit_adder_12_c_out), .Sum(Sum[12]), .C_out(n1_bit_adder_13_c_out));
  _1_bit_adder u_1_bit_adder_14 (
    .A(A[13]), .B(B[13]), .C_in(n1_bit_adder_13_c_out), .Sum(Sum[13]), .C_out(n1_bit_adder_14_c_out));
  _1_bit_adder u_1_bit_adder_15 (
    .A(A[14]), .B(B[14]), .C_in(n1_bit_adder_14_c_out), .Sum(Sum[14]), .C_out(n1_bit_adder_15_c_out));
  _1_bit_adder u_1_bit_adder_16 (
    .A(A[15]), .B(B[15]), .C_in(n1_bit_adder_15_c_out), .Sum(Sum[15]), .C_out(n1_bit_adder_16_c_out));
  _1_bit_adder u_1_bit_adder_17 (
    .A(A[16]), .B(B[16]), .C_in(n1_bit_adder_16_c_out), .Sum(Sum[16]), .C_out(n1_bit_adder_17_c_out));
  _1_bit_adder u_1_bit_adder_18 (
    .A(A[17]), .B(B[17]), .C_in(n1_bit_adder_17_c_out), .Sum(Sum[17]), .C_out(n1_bit_adder_18_c_out));
  _1_bit_adder u_1_bit_adder_19 (
    .A(A[18]), .B(B[18]), .C_in(n1_bit_adder_18_c_out), .Sum(Sum[18]), .C_out(n1_bit_adder_19_c_out));
  _1_bit_adder u_1_bit_adder_20 (
    .A(A[19]), .B(B[19]), .C_in(n1_bit_adder_19_c_out), .Sum(Sum[19]), .C_out(n1_bit_adder_20_c_out));
  _1_bit_adder u_1_bit_adder_21 (
    .A(A[20]), .B(B[20]), .C_in(n1_bit_adder_20_c_out), .Sum(Sum[20]), .C_out(n1_bit_adder_21_c_out));
  _1_bit_adder u_1_bit_adder_22 (
    .A(A[21]), .B(B[21]), .C_in(n1_bit_adder_21_c_out), .Sum(Sum[21]), .C_out(n1_bit_adder_22_c_out));
  _1_bit_adder u_1_bit_adder_23 (
    .A(A[22]), .B(B[22]), .C_in(n1_bit_adder_22_c_out), .Sum(Sum[22]), .C_out(n1_bit_adder_23_c_out));
  _1_bit_adder u_1_bit_adder_24 (
    .A(A[23]), .B(B[23]), .C_in(n1_bit_adder_23_c_out), .Sum(Sum[23]), .C_out(n1_bit_adder_24_c_out));
  _1_bit_adder u_1_bit_adder_25 (
    .A(A[24]), .B(B[24]), .C_in(n1_bit_adder_24_c_out), .Sum(Sum[24]), .C_out(n1_bit_adder_25_c_out));
  _1_bit_adder u_1_bit_adder_26 (
    .A(A[25]), .B(B[25]), .C_in(n1_bit_adder_25_c_out), .Sum(Sum[25]), .C_out(n1_bit_adder_26_c_out));
  _1_bit_adder u_1_bit_adder_27 (
    .A(A[26]), .B(B[26]), .C_in(n1_bit_adder_26_c_out), .Sum(Sum[26]), .C_out(n1_bit_adder_27_c_out));
  _1_bit_adder u_1_bit_adder_28 (
    .A(A[27]), .B(B[27]), .C_in(n1_bit_adder_27_c_out), .Sum(Sum[27]), .C_out(n1_bit_adder_28_c_out));
  _1_bit_adder u_1_bit_adder_29 (
    .A(A[28]), .B(B[28]), .C_in(n1_bit_adder_28_c_out), .Sum(Sum[28]), .C_out(n1_bit_adder_29_c_out));
  _1_bit_adder u_1_bit_adder_30 (
    .A(A[29]), .B(B[29]), .C_in(n1_bit_adder_29_c_out), .Sum(Sum[29]), .C_out(n1_bit_adder_30_c_out));
  _1_bit_adder u_1_bit_adder_31 (
    .A(A[30]), .B(B[30]), .C_in(n1_bit_adder_30_c_out), .Sum(Sum[30]), .C_out(n1_bit_adder_31_c_out));
  _1_bit_adder u_1_bit_adder_32 (.A(A[31]), .B(B[31]), .C_in(n1_bit_adder_31_c_out), .Sum(Sum[31]), .C_out(C_out));
endmodule

module _64_bit_shifter (
  input  [31:0] Product,
  input  [31:0] Multiplier,
  input  Cout,
  output [31:0] Product_2,
  output [31:0] Multiplier_2
);


  assign Multiplier_2 = {Product[0], Multiplier[31:1]};
  assign Product_2 = {Cout, Product[31:1]};
endmodule

module _6_bit_adder (
  input  [5:0] A,
  input  [5:0] B,
  output C_out,
  output [5:0] Sum
);

  wire n1_bit_adder_1_c_out, n1_bit_adder_2_c_out, n1_bit_adder_3_c_out, n1_bit_adder_4_c_out,
       n1_bit_adder_5_c_out;

  _1_bit_adder u_1_bit_adder_1 (.A(A[0]), .B(B[0]), .C_in(1'b0), .Sum(Sum[0]), .C_out(n1_bit_adder_1_c_out));
  _1_bit_adder u_1_bit_adder_2 (
    .A(A[1]), .B(B[1]), .C_in(n1_bit_adder_1_c_out), .Sum(Sum[1]), .C_out(n1_bit_adder_2_c_out));
  _1_bit_adder u_1_bit_adder_3 (
    .A(A[2]), .B(B[2]), .C_in(n1_bit_adder_2_c_out), .Sum(Sum[2]), .C_out(n1_bit_adder_3_c_out));
  _1_bit_adder u_1_bit_adder_4 (
    .A(A[3]), .B(B[3]), .C_in(n1_bit_adder_3_c_out), .Sum(Sum[3]), .C_out(n1_bit_adder_4_c_out));
  _1_bit_adder u_1_bit_adder_5 (
    .A(A[4]), .B(B[4]), .C_in(n1_bit_adder_4_c_out), .Sum(Sum[4]), .C_out(n1_bit_adder_5_c_out));
  _1_bit_adder u_1_bit_adder_6 (.A(A[5]), .B(B[5]), .C_in(n1_bit_adder_5_c_out), .Sum(Sum[5]), .C_out(C_out));
endmodule

module equal (
  input  [5:0] A,
  input  [5:0] B,
  output Sum
);

  wire xnor_1_out, xnor_2_out, xnor_3_out, xnor_4_out, xnor_5_out, xnor_6_out;

  xnor xnor_1 (xnor_1_out, A[0], B[0]);
  xnor xnor_2 (xnor_2_out, A[1], B[1]);
  xnor xnor_3 (xnor_3_out, A[2], B[2]);
  xnor xnor_4 (xnor_4_out, A[3], B[3]);
  xnor xnor_5 (xnor_5_out, A[4], B[4]);
  xnor xnor_6 (xnor_6_out, A[5], B[5]);
  and and_1 (Sum, xnor_1_out, xnor_2_out, xnor_3_out, xnor_4_out, xnor_5_out, xnor_6_out);
endmodule
