// Logisim project mult32.circ as structural Verilog: 1 circuit, main circuit main
module main (
  input  [31:0] Multiplicand,
  input  [31:0] Multiplier,
  input  START,
  output [31:0] out_4,
  output [31:0] out_5
);

  wire clock_1_out, main_1_lcontrol, main_1_lcout, main_1_lmultiplicand, main_1_lmultiplier, main_1_lproduct,
       main_1_scontrol, main_1_scout, main_1_smultiplier, main_2_equal, main_2_product1;
  wire [1:0] main_1_sproduct;

  Clock clock_1 (.out(clock_1_out));
  control_main main_1 (
    .Go(START), .Equal(main_2_equal), .product1(main_2_product1), .CLK(clock_1_out),
    .lMultiplicand(main_1_lmultiplicand), .lMultiplier(main_1_lmultiplier), .sMultiplier(main_1_smultiplier),
    .lProduct(main_1_lproduct), .sProduct(main_1_sproduct), .lControl(main_1_lcontrol),
    .sControl(main_1_scontrol), .lCout(main_1_lcout), .sCout(main_1_scout));
  datapath_main main_2 (
    .Multiplicand(Multiplicand), .lMultiplicand(main_1_lmultiplicand), .Multiplier(Multiplier),
    .Clock(clock_1_out), .sControl(main_1_scontrol), .sMultiplier(main_1_smultiplier),
    .lControl(main_1_lcontrol), .sProduct(main_1_sproduct), .lProduct(main_1_lproduct),
    .lMultiplier(main_1_lmultiplier), .sCout(main_1_scout), .lcout(main_1_lcout), .product1(main_2_product1),
    .RESULTM(out_5), .RESULTP(out_4), .Equal(main_2_equal));

  // Notes on the sheet:
  //   RESULT
endmodule
